// Logisim project AndrewCPU.circ as structural Verilog: 5 circuits, main circuit ALU
module ALU (
  input  [7:0] A,
  input  [7:0] B,
  input  [2:0] in_3,
  output [7:0] Result
);

  wire [7:0] adder_1_out, adder_2_out, adder_3_out, and_1_out, or_1_out, subtractor_1_out;

  assign and_1_out = A & B;  // AND_Gate and_1, 8 bits wide
  assign or_1_out = A | B;  // OR_Gate or_1, 8 bits wide
  Adder adder_1 (.a(A), .b(8'h1), .out(adder_1_out));  // open: cin, cout
  Adder adder_2 (.a(B), .b(8'h1), .out(adder_2_out));  // open: cin, cout
  Adder adder_3 (.a(A), .b(B), .out(adder_3_out));  // open: cin, cout
  Subtractor subtractor_1 (.a(A), .b(B), .out(subtractor_1_out));  // open: bin, bout
  Multiplexer #(.select(3), .width(8), .enable("false")) multiplexer_1 (
    .in0(A), .in1(B), .in2(adder_1_out), .in3(adder_2_out), .in4(adder_3_out), .in5(subtractor_1_out),
    .in6(and_1_out), .in7(or_1_out), .out(Result), .sel(in_3));
endmodule

// CPU
module main (
  input  [7:0] ram,
  input  [7:0] pc,
  input  reset,
  input  [7:0] in,
  output [7:0] out
);

  wire [1:0] control_unit_1_b;
  wire [2:0] control_unit_1_aluop;
  wire [4:0] control_unit_1_regwrite;
  wire [7:0] ALU_result, multiplexer_1_out, registers_a, registers_b, registers_mbr;

  Control_Unit control_unit_1 (
    .mbr(registers_mbr), .b(control_unit_1_b), .regwrite(control_unit_1_regwrite),
    .aluop(control_unit_1_aluop));
  registers registers (
    .data(ALU_result), .external(ram), .regwrite(control_unit_1_regwrite), .clear(reset), .a(registers_a),
    .b(registers_b), .out(out), .mbr(registers_mbr), .pc(pc));
  Multiplexer #(.select(2), .width(8), .enable("false")) multiplexer_1 (
    .in0(registers_b), .in1(registers_mbr), .in2(pc), .in3(in), .out(multiplexer_1_out),
    .sel(control_unit_1_b));
  ALU ALU (.A(registers_a), .B(multiplexer_1_out), .in_3(control_unit_1_aluop), .Result(ALU_result));
endmodule

module registers (
  input  [7:0] data,
  input  [7:0] external,
  input  [4:0] regwrite,
  input  clear,
  output [7:0] a,
  output [7:0] b,
  output [7:0] out,
  output [7:0] mbr,
  output [7:0] pc
);

  wire [7:0] multiplexer_1_out;

  Multiplexer #(.width(8), .enable("false")) multiplexer_1 (
    .in0(data), .in1(external), .out(multiplexer_1_out), .sel(regwrite[0]));
  Register u_A (.D(multiplexer_1_out), .Q(a), .clk(regwrite[4]), .clr(clear));  // open: en
  Register u_B (.D(multiplexer_1_out), .Q(b), .clk(regwrite[3]), .clr(clear));  // open: en
  Register u_OUT (.D(multiplexer_1_out), .Q(out), .clk(regwrite[2]), .clr(clear));  // open: en
  Register u_MBR (.D(multiplexer_1_out), .Q(mbr), .clk(regwrite[0]), .clr(clear));  // open: en
  Register u_PC (.D(multiplexer_1_out), .Q(pc), .clk(regwrite[1]), .clr(clear));  // open: en
endmodule

// CU
module Control_Unit (
  input  [7:0] mbr,
  output [1:0] b,
  output [4:0] regwrite,
  output [2:0] aluop
);

  wire clock_1_out;
  wire [4:0] MPC_q, multiplexer_1_out;
  wire [15:0] ram_1_data;
  wire [15:10] MIR_q;

  Multiplexer #(.width(5), .enable("false")) multiplexer_1 (
    .in0(MIR_q[15:11]), .in1(mbr[4:0]), .out(multiplexer_1_out), .sel(MIR_q[10]));
  Register #(.width(5)) MPC (.D(multiplexer_1_out), .Q(MPC_q), .clk(clock_1_out));  // open: en, clr
  Clock clock_1 (.out(clock_1_out));
  RAM #(.addrWidth(5), .dataWidth(16), .bus("asynch")) ram_1 (.addr(MPC_q), .data(ram_1_data));  // open: sel, ld, clr
  Register #(.width(16)) MIR (.D(ram_1_data), .Q({MIR_q, aluop, regwrite, b}), .clk(clock_1_out));  // open: en, clr
endmodule

module io (
  input  in_1
);

  wire [3:0] main_1_out, main_1_out_2;
  wire [7:0] _0_out, ram_1_data, undriven;

  RAM ram_1 (.addr(undriven), .data(ram_1_data));  // open: sel, clk, ld, clr
  main main_1 (.ram(ram_1_data), .reset(in_1), .out({main_1_out_2, main_1_out}), .pc(undriven), .in(_0_out));
  Hex_Digit_Display hex_digit_display_1 (.value(main_1_out_2));  // open: dp
  Hex_Digit_Display hex_digit_display_2 (.value(main_1_out));  // open: dp
  Button _0 (.out(_0_out[0]));
  Button _1 (.out(_0_out[1]));
  Button _2 (.out(_0_out[2]));
  Button _3 (.out(_0_out[3]));
  Button _4 (.out(_0_out[4]));
  Button _5 (.out(_0_out[5]));
  Button _6 (.out(_0_out[6]));
  Button _7 (.out(_0_out[7]));
endmodule
