// Logisim project datapath.circ as structural Verilog: 3 circuits, main circuit main
module main (
);

  wire [1:0] undriven;
  wire [7:0] _0_out, ALU_result, multiplexer_1_out, registers_1_a, registers_1_b, registers_1_mbr,
       registers_1_out, registers_1_pc;

  Button _1 (.out(_0_out[1]));
  Button _0 (.out(_0_out[0]));
  Button _2 (.out(_0_out[2]));
  Button _6 (.out(_0_out[6]));
  Button _3 (.out(_0_out[3]));
  Button _4 (.out(_0_out[4]));
  Button _5 (.out(_0_out[5]));
  registers registers_1 (
    .data(ALU_result), .a(registers_1_a), .b(registers_1_b), .out(registers_1_out), .mbr(registers_1_mbr),
    .pc(registers_1_pc));  // open: write, reg, clear
  Button _7 (.out(_0_out[7]));
  Multiplexer #(.select(2), .width(8), .enable("false")) multiplexer_1 (
    .in0(registers_1_b), .in1(registers_1_mbr), .in2(registers_1_pc), .in3(_0_out), .out(multiplexer_1_out),
    .sel(undriven));
  Hex_Digit_Display hex_digit_display_1 (.value(registers_1_out[3:0]));  // open: dp
  Hex_Digit_Display hex_digit_display_2 (.value(registers_1_out[7:4]));  // open: dp
  ALU ALU (.A(registers_1_a), .B(multiplexer_1_out), .Result(ALU_result));  // open: in_3

  // Notes on the sheet:
  //   B Bus select lines
  //   External Memory Address Bus
endmodule

module ALU (
  input  [7:0] A,
  input  [7:0] B,
  input  [2:0] in_3,
  output [7:0] Result
);

  wire [7:0] adder_1_out, adder_2_out, adder_3_out, and_1_out, or_1_out, subtractor_1_out;

  assign and_1_out = A & B;  // AND_Gate and_1, 8 bits wide
  assign or_1_out = A | B;  // OR_Gate or_1, 8 bits wide
  Adder adder_1 (.a(A), .b(8'h1), .out(adder_1_out));  // open: cin, cout
  Adder adder_2 (.a(B), .b(8'h1), .out(adder_2_out));  // open: cin, cout
  Adder adder_3 (.a(A), .b(B), .out(adder_3_out));  // open: cin, cout
  Subtractor subtractor_1 (.a(A), .b(B), .out(subtractor_1_out));  // open: bin, bout
  Multiplexer #(.select(3), .width(8), .enable("false")) multiplexer_1 (
    .in0(A), .in1(B), .in2(adder_1_out), .in3(adder_2_out), .in4(adder_3_out), .in5(subtractor_1_out),
    .in6(and_1_out), .in7(or_1_out), .out(Result), .sel(in_3));
endmodule

module registers (
  input  [7:0] data,
  input  write,
  input  [2:0] \reg ,
  input  clear,
  output [7:0] a,
  output [7:0] b,
  output [7:0] out,
  output [7:0] mbr,
  output [7:0] pc
);

  wire demultiplexer_1_out0, demultiplexer_1_out1, demultiplexer_1_out2, demultiplexer_1_out3,
       demultiplexer_1_out4;

  Demultiplexer #(.select(3), .enable("false")) demultiplexer_1 (
    .out0(demultiplexer_1_out0), .out1(demultiplexer_1_out1), .out2(demultiplexer_1_out2),
    .out3(demultiplexer_1_out3), .out4(demultiplexer_1_out4), .in(write), .sel(\reg ));  // open: out5, out6, out7
  Register u_A (.D(data), .Q(a), .clk(demultiplexer_1_out0), .clr(clear));  // open: en
  Register u_B (.D(data), .Q(b), .clk(demultiplexer_1_out1), .clr(clear));  // open: en
  Register u_OUT (.D(data), .Q(out), .clk(demultiplexer_1_out2), .clr(clear));  // open: en
  Register u_MBR (.D(data), .Q(mbr), .clk(demultiplexer_1_out3), .clr(clear));  // open: en
  Register u_PC (.D(data), .Q(pc), .clk(demultiplexer_1_out4), .clr(clear));  // open: en
endmodule
