// Logisim project registers.circ as structural Verilog: 2 circuits, main circuit main
module main (
);

  registers registers_1 ();  // open: data, write, reg, clear, a, b, out, mbr, pc, mir, mpc
endmodule

module registers (
  input  [7:0] data,
  input  write,
  input  [2:0] \reg ,
  input  clear,
  output [7:0] a,
  output [7:0] b,
  output [7:0] out,
  output [7:0] mbr,
  output [7:0] pc,
  output [7:0] mir,
  output [7:0] mpc
);

  wire demultiplexer_1_out0, demultiplexer_1_out1, demultiplexer_1_out2, demultiplexer_1_out3,
       demultiplexer_1_out4, demultiplexer_1_out5, demultiplexer_1_out6;

  Demultiplexer #(.select(3), .enable("false")) demultiplexer_1 (
    .out0(demultiplexer_1_out0), .out1(demultiplexer_1_out1), .out2(demultiplexer_1_out2),
    .out3(demultiplexer_1_out3), .out4(demultiplexer_1_out4), .out5(demultiplexer_1_out5),
    .out6(demultiplexer_1_out6), .in(write), .sel(\reg ));  // open: out7
  Register u_A (.D(data), .Q(a), .clk(demultiplexer_1_out0), .clr(clear));  // open: en
  Register u_B (.D(data), .Q(b), .clk(demultiplexer_1_out1), .clr(clear));  // open: en
  Register u_OUT (.D(data), .Q(out), .clk(demultiplexer_1_out2), .clr(clear));  // open: en
  Register u_MBR (.D(data), .Q(mbr), .clk(demultiplexer_1_out3), .clr(clear));  // open: en
  Register u_PC (.D(data), .Q(pc), .clk(demultiplexer_1_out4), .clr(clear));  // open: en
  Register u_MIR (.D(data), .Q(mir), .clk(demultiplexer_1_out5), .clr(clear));  // open: en
  Register u_MPC (.D(data), .Q(mpc), .clk(demultiplexer_1_out6), .clr(clear));  // open: en
endmodule
